# Fritzing sketch ADXL345_Testing (saved by Fritzing 0.9.3b)

parts:
  元件3 = Triple Axis Accelerometer Breakout - ADXL345
  元件4 = Arduino Leonardo (Rev3b)
  元件6 = Triple Axis Accelerometer Breakout - ADXL345
  元件7 = Arduino Nano (Rev3.0)

nets:
  GND: 元件3.GND, 元件4.GND
  VCC: 元件3.VCC, 元件4.3V3
  N1: 元件3.SDA, 元件4.A4
  N2: 元件3.SCL, 元件4.A5
  GND_2: 元件6.GND, 元件7.GND, 元件7.D2
  VCC_2: 元件6.VCC, 元件7.3V3, 元件7.D13/SCK
  N3: 元件6.SDA, 元件7.A4, 元件7.A3
  N4: 元件6.SCL, 元件7.A5

notes:
  NANO 连线图
  UNO 连线图
  ADXL345
