# Fritzing sketch Fenbei (saved by Fritzing 0.9.3b)
breadboards: 1

parts:
  LED1 = RGB LED (com. cathode, rgb) [package="5 mm [THT]"]
  MIC1 = Microphone
  LED2 = LED - 5mm [color="Red (633nm)" package="5 mm [THT]"]
  R1 = Resistor [tolerance=±5% resistance=220 package=THT]
  LED3 = LED - 5mm [color="Red (633nm)" package="5 mm [THT]"]
  R2 = Resistor [tolerance=±5% resistance=220 package=THT]
  R3 = Resistor [tolerance=±5% resistance=220 package=THT]
  LED4 = LED - 5mm [color="Red (633nm)" package="5 mm [THT]"]
  R4 = Resistor [tolerance=±5% resistance=220 package=THT]
  LED5 = LED - 5mm [color="Red (633nm)" package="5 mm [THT]"]
  R5 = Resistor [tolerance=±5% resistance=220 package=THT]
  LED6 = LED - 5mm [color="Red (633nm)" package="5 mm [THT]"]
  R6 = Resistor [tolerance=±5% resistance=220 package=THT]
  LED7 = LED - 5mm [color="Red (633nm)" package="5 mm [THT]"]
  R7 = Resistor [tolerance=±5% resistance=220 package=THT]
  LED8 = LED - 5mm [color="Red (633nm)" package="5 mm [THT]"]
  R8 = Resistor [tolerance=±5% resistance=220 package=THT]
  LED9 = LED - 5mm [color="Red (633nm)" package="5 mm [THT]"]
  R9 = Resistor [tolerance=±5% resistance=220 package=THT]
  LED10 = LED - 5mm [color="Red (633nm)" package="5 mm [THT]"]
  元件1 = Arduino Uno (Rev3) - ICSP

nets:
  N1: LED1.red_anode, 元件1.A0
  N2: LED1.common_cathode, MIC1.pin1, LED2.cathode, LED3.cathode, LED4.cathode, LED5.cathode, LED6.cathode, LED7.cathode, LED8.cathode, LED9.cathode, LED10.cathode, 元件1.GND
  N3: LED1.green_anode, MIC1.pin2, 元件1.5V
  N4: LED2.anode, R1.Pin_0
  N5: R1.Pin_1, 元件1.D9_PWM
  N6: LED3.anode, R2.Pin_0
  N7: R2.Pin_1, 元件1.D8
  N8: R3.Pin_0, LED4.anode
  N9: R3.Pin_1, 元件1.D7
  N10: R4.Pin_0, LED5.anode
  N11: R4.Pin_1, 元件1.D6_PWM
  N12: R5.Pin_0, LED6.anode
  N13: R5.Pin_1, 元件1.D5_PWM
  N14: R6.Pin_0, LED7.anode
  N15: R6.Pin_1, 元件1.D4
  N16: R7.Pin_0, LED8.anode
  N17: R7.Pin_1, 元件1.D3_PWM
  N18: R8.Pin_0, LED9.anode
  N19: R8.Pin_1, 元件1.D2
  N20: R9.Pin_0, LED10.anode
  N21: R9.Pin_1, 元件1.D1/TX
