# Fritzing sketch Heartbeat_Test (saved by Fritzing 0.9.3b)
breadboards: 1

parts:
  元件1 = Arduino Nano (Rev3.0)
  Q1 = PNP-Transistor [package="TO92 [THT]"]
  元件2 = Arduino Uno (Rev3)
  Q2 = PNP-Transistor [package="TO92 [THT]"]

nets:
  N1: 元件1.GND, Q1.C
  N2: 元件1.D4, Q1.E
  N3: 元件1.5V, Q1.B
  N4: 元件2.D4, Q2.E
  N5: 元件2.5V, Q2.B
  N6: 元件2.GND, Q2.C

notes:
  Heartbeat
  left: Sign (Pin:D4)
  midd: VCC(5v)
  right: Gnd
