# Fritzing sketch SanYuanSe_demo (saved by Fritzing 0.9.3b)
perfboards: 1

parts:
  R1 = Rotary Potentiometer (Small) [maximum_resistance=100kΩ package=THT]
  R2 = Rotary Potentiometer (Small) [maximum_resistance=100kΩ package=THT]
  R3 = Rotary Potentiometer (Small) [maximum_resistance=100kΩ package=THT]
  LED1 = RGB LED (com. cathode, rgb) [package="5 mm [THT]"]  # not connected
  元件1 = Arduino Uno (Rev3) - ICSP
  LED2 = RGB LED (com. cathode, rgb) [package="5 mm [THT]"]
  LED3 = RGB LED (com. cathode, rgb) [package="5 mm [THT]"]
  LED4 = RGB LED (com. cathode, rgb) [package="5 mm [THT]"]
  R4 = Resistor [tolerance=±5% resistance=220 package=THT]
  R5 = Resistor [tolerance=±5% resistance=220 package=THT]
  R6 = Resistor [tolerance=±5% resistance=220 package=THT]
  R7 = Resistor [tolerance=±5% resistance=220 package=THT]
  R8 = Resistor [tolerance=±5% resistance=220 package=THT]
  R9 = Resistor [tolerance=±5% resistance=220 package=THT]

nets:
  N1: R1.wiper, 元件1.A0
  N2: R2.wiper, 元件1.A1
  N3: R3.leg1, 元件1.5V
  N4: R3.wiper, 元件1.A2
  N5: 元件1.D3_PWM, R4.Pin_1
  N6: 元件1.D5_PWM, R7.Pin_1
  N7: 元件1.D6_PWM, R9.Pin_1
  N8: 元件1.GND, LED4.common_cathode
  N9: LED2.green_anode, R7.Pin_0
  N10: LED3.blue_anode, R9.Pin_0
  N11: LED4.red_anode, R5.Pin_1
  N12: LED4.green_anode, R6.Pin_0
  N13: LED4.blue_anode, R8.Pin_0
