# Fritzing sketch BizhangCar (saved by Fritzing 0.9.3b)
perfboards: 1

parts:
  元件4 = Arduino Nano (Rev3.0)
  元件5 = NRF24L01+ Breakout Board

nets:
  N1: 元件4.D7, 元件5.CS
  N2: 元件4.D8, 元件5.CE
  N3: 元件4.D11/MOSI, 元件5.MOSI
  N4: 元件4.D12/MISO, 元件5.MISO
  3V3: 元件4.3V3, 元件5.VCC
  N5: 元件4.D13/SCK, 元件5.SCK

notes:
  NRF24L01_Sender
  输出1-4，电机驱动输出
