# Fritzing sketch AutoCar (saved by Fritzing 0.9.3b)
perfboards: 1

parts:
  元件1 = Arduino Nano (Rev3.0)
  M1 = DC Motor
  M2 = DC Motor
  BAT1 = BC9VPC [package=bc9vpc]
  S2 = Round Pushbutton
  S3 = Round Pushbutton
  R1 = Rotary Potentiometer (Small) [maximum_resistance=100kΩ package=THT]
  R2 = Rotary Potentiometer (Small) [maximum_resistance=100kΩ package=THT]
  S4 = Round Pushbutton  # not connected

nets:
  N1: 元件1.GND, R2.leg1
  N2: M1.pin_2, R1.wiper
  N3: M2.pin_2, R2.wiper
  N4: BAT1.V+, S2.leg0
  N5: S2.leg1, S3.leg1

notes:
  L298n
  A1 in1
  A2 in2
  B1 in3
  B2 in4
  Vin
  Gnd
  彩灯开关
  电机开关
  总开关
  彩灯
  Gnd Din Vcc
