# Fritzing sketch Big_Led (saved by Fritzing 0.9.3b)
breadboards: 1

parts:
  RGB_SMD_LED1 = SMD RGB LED (WS2812) [package=5050]
  元件1 = Arduino Leonardo (Rev3b)
  RGB_SMD_LED2 = SMD RGB LED (WS2812) [package=5050]
  RGB_SMD_LED3 = SMD RGB LED (WS2812) [package=5050]
  RGB_SMD_LED4 = SMD RGB LED (WS2812) [package=5050]
  RGB_SMD_LED5 = SMD RGB LED (WS2812) [package=5050]
  RGB_SMD_LED6 = SMD RGB LED (WS2812) [package=5050]
  RGB_SMD_LED7 = SMD RGB LED (WS2812) [package=5050]
  RGB_SMD_LED8 = SMD RGB LED (WS2812) [package=5050]
  RGB_SMD_LED14 = SMD RGB LED (WS2812) [package=5050]
  RGB_SMD_LED18 = SMD RGB LED (WS2812) [package=5050]
  RGB_SMD_LED20 = SMD RGB LED (WS2812) [package=5050]
  RGB_SMD_LED35 = SMD RGB LED (WS2812) [package=5050]
  RGB_SMD_LED43 = SMD RGB LED (WS2812) [package=5050]
  RGB_SMD_LED57 = SMD RGB LED (WS2812) [package=5050]
  RGB_SMD_LED60 = SMD RGB LED (WS2812) [package=5050]
  RGB_SMD_LED69 = SMD RGB LED (WS2812) [package=5050]
  RGB_SMD_LED75 = SMD RGB LED (WS2812) [package=5050]
  RGB_SMD_LED83 = SMD RGB LED (WS2812) [package=5050]
  RGB_SMD_LED92 = SMD RGB LED (WS2812) [package=5050]
  RGB_SMD_LED93 = SMD RGB LED (WS2812) [package=5050]
  RGB_SMD_LED102 = SMD RGB LED (WS2812) [package=5050]
  RGB_SMD_LED110 = SMD RGB LED (WS2812) [package=5050]
  RGB_SMD_LED117 = SMD RGB LED (WS2812) [package=5050]
  microSD_Transflash1 = SparkFun - microSD Transflash

nets:
  N1: RGB_SMD_LED1.DOut, 元件1.GND, RGB_SMD_LED20.DOut, RGB_SMD_LED35.DOut, RGB_SMD_LED43.DOut, microSD_Transflash1.CS
  N2: RGB_SMD_LED1.DIn, 元件1.D3_PWM/SCL
  VCC: RGB_SMD_LED1.VCC, RGB_SMD_LED14.VCC, RGB_SMD_LED18.VCC, RGB_SMD_LED20.VCC, RGB_SMD_LED35.VCC, RGB_SMD_LED43.VCC, RGB_SMD_LED57.VCC, RGB_SMD_LED60.VCC
  N3: RGB_SMD_LED1.NC, RGB_SMD_LED2.VCC
  N4: RGB_SMD_LED1.VDD, RGB_SMD_LED2.DIn
  N5: RGB_SMD_LED1.VSS, RGB_SMD_LED2.DOut
  N6: 元件1.D4/A6, RGB_SMD_LED14.DIn
  N7: 元件1.D5_PWM, RGB_SMD_LED20.DIn
  N8: 元件1.D6_PWM/A7, RGB_SMD_LED18.DIn
  N9: 元件1.D7, RGB_SMD_LED35.DIn
  N10: 元件1.3V3, microSD_Transflash1.DI
  N11: 元件1.A0, microSD_Transflash1.DO
  N12: 元件1.D8/A8, RGB_SMD_LED60.DIn
  N13: 元件1.D9_PWM/A9, RGB_SMD_LED43.DIn
  N14: 元件1.D10_PWM/A10, RGB_SMD_LED57.DIn
  N15: 元件1.D11_PWM, microSD_Transflash1.SCK
  N16: 元件1.D12/A11, microSD_Transflash1.VCC
  N17: 元件1.D13_PWM, microSD_Transflash1.GND
  N18: RGB_SMD_LED2.NC, RGB_SMD_LED3.VCC
  N19: RGB_SMD_LED2.VDD, RGB_SMD_LED3.DIn
  N20: RGB_SMD_LED2.VSS, RGB_SMD_LED3.DOut
  N21: RGB_SMD_LED3.NC, RGB_SMD_LED4.VCC
  N22: RGB_SMD_LED3.VDD, RGB_SMD_LED4.DIn
  N23: RGB_SMD_LED3.VSS, RGB_SMD_LED4.DOut
  N24: RGB_SMD_LED4.NC, RGB_SMD_LED7.VCC
  N25: RGB_SMD_LED4.VDD, RGB_SMD_LED7.DIn
  N26: RGB_SMD_LED4.VSS, RGB_SMD_LED7.DOut
  N27: RGB_SMD_LED5.DOut, RGB_SMD_LED6.VSS
  N28: RGB_SMD_LED5.DIn, RGB_SMD_LED6.VDD
  N29: RGB_SMD_LED5.VCC, RGB_SMD_LED6.NC
  N30: RGB_SMD_LED6.DOut, RGB_SMD_LED8.VSS
  N31: RGB_SMD_LED6.DIn, RGB_SMD_LED8.VDD
  N32: RGB_SMD_LED6.VCC, RGB_SMD_LED8.NC
  N33: RGB_SMD_LED7.NC, RGB_SMD_LED8.VCC
  N34: RGB_SMD_LED7.VDD, RGB_SMD_LED8.DIn
  N35: RGB_SMD_LED7.VSS, RGB_SMD_LED8.DOut
  N36: RGB_SMD_LED69.DOut, RGB_SMD_LED75.VSS
  N37: RGB_SMD_LED69.DIn, RGB_SMD_LED75.VDD
  N38: RGB_SMD_LED69.VCC, RGB_SMD_LED75.NC
  N39: RGB_SMD_LED69.NC, RGB_SMD_LED93.VCC
  N40: RGB_SMD_LED69.VDD, RGB_SMD_LED93.DIn
  N41: RGB_SMD_LED69.VSS, RGB_SMD_LED93.DOut
  N42: RGB_SMD_LED75.DOut, RGB_SMD_LED117.VSS
  N43: RGB_SMD_LED75.DIn, RGB_SMD_LED117.VDD
  N44: RGB_SMD_LED75.VCC, RGB_SMD_LED117.NC
  N45: RGB_SMD_LED83.DOut, RGB_SMD_LED93.VSS
  N46: RGB_SMD_LED83.DIn, RGB_SMD_LED93.VDD
  N47: RGB_SMD_LED83.VCC, RGB_SMD_LED93.NC
  N48: RGB_SMD_LED83.NC, RGB_SMD_LED110.VCC
  N49: RGB_SMD_LED83.VDD, RGB_SMD_LED110.DIn
  N50: RGB_SMD_LED83.VSS, RGB_SMD_LED110.DOut
  N51: RGB_SMD_LED92.DOut, RGB_SMD_LED102.VSS
  N52: RGB_SMD_LED92.DIn, RGB_SMD_LED102.VDD
  N53: RGB_SMD_LED92.VCC, RGB_SMD_LED102.NC
  N54: RGB_SMD_LED92.NC, RGB_SMD_LED117.VCC
  N55: RGB_SMD_LED92.VDD, RGB_SMD_LED117.DIn
  N56: RGB_SMD_LED92.VSS, RGB_SMD_LED117.DOut

notes:
  GND
  VCC
  MOSO
  MOSI
  SCK
  CS
