# Fritzing sketch ChaoShengBo_LED (saved by Fritzing 0.9.3b)
breadboards: 1

parts:
  元件1 = Arduino Nano (Rev3.0) (ICSP)
  Peppermill_Power_Board1 = Peppermill Power Board
  hc-sr1 = hc-sr04

nets:
  GND: 元件1.GND, Peppermill_Power_Board1.V+, hc-sr1.GND
  N1: 元件1.D2, Peppermill_Power_Board1.PGC
  N2: 元件1.D3, Peppermill_Power_Board1.PGD
  N3: 元件1.D4, Peppermill_Power_Board1.GPIO
  N4: 元件1.D5, Peppermill_Power_Board1.Ground
  N5: 元件1.D7, hc-sr1.Echo
  N6: 元件1.D8, hc-sr1.Trig
  N7: 元件1.D9, Peppermill_Power_Board1.VPP
  5V: 元件1.5V, hc-sr1.VCC
  N8: 元件1.3V3, Peppermill_Power_Board1.Direction

notes:
  ---- Nokia 5110 LCD ----
  PGD: RST PGC: CE
  VPP: DC GND: Din
  GPIO: Clk SPEED:Vcc
  DIRECTION:BL V+:Gnd
