# Fritzing sketch NRF24L01_Sender (saved by Fritzing 0.9.3b)
breadboards: 1

parts:
  元件1 = Arduino Nano (Rev3.0) (ICSP)
  元件2 = Thumb Joystick
  元件3 = NRF24L01+ Breakout Board
  Peppermill_Power_Board1 = Peppermill Power Board
  S1 = Pushbutton [package="[THT]"]
  S2 = Pushbutton [package="[THT]"]

nets:
  GND: 元件1.GND, 元件2.GND, 元件3.GND, Peppermill_Power_Board1.V+, S1.Pin_3, S1.Pin_4, S2.Pin_3, S2.Pin_4
  N1: 元件1.D2, Peppermill_Power_Board1.PGC
  N2: 元件1.D3, Peppermill_Power_Board1.PGD
  N3: 元件1.D4, Peppermill_Power_Board1.GPIO
  N4: 元件1.D5, Peppermill_Power_Board1.Ground
  N5: 元件1.D7, 元件3.CS
  N6: 元件1.D8, 元件3.CE
  N7: 元件1.D9, Peppermill_Power_Board1.VPP
  N8: 元件1.D11/MOSI, 元件3.MOSI
  N9: 元件1.D12/MISO, 元件3.MISO
  VCC: 元件1.5V, 元件2.VCC, 元件3.VCC
  N10: 元件1.A7, S2.Pin_1, S2.Pin_2
  N11: 元件1.A6, S1.Pin_1, S1.Pin_2
  N12: 元件1.A2, 元件2.VERT
  N13: 元件1.A1, 元件2.HORZ
  N14: 元件1.A0, 元件2.SEL
  N15: 元件1.3V3, Peppermill_Power_Board1.Direction
  N16: 元件1.D13/SCK, 元件3.SCK

notes:
  VCC:VCC
  VER :VRX
  HOF:VRY
  SEL :SW
  GND:GND
  ---- Nokia 5110 LCD ----
  PGD: RST PGC: CE
  VPP: DC GND: Din
  GPIO: Clk SPEED:Vcc
  DIRECTION:BL V+:Gnd
  NRF24L01_Sender
