# Fritzing sketch Fire Sensor (saved by Fritzing 0.9.3b)
perfboards: 1

parts:
  J1 = Piezo Speaker
  元件1 = Arduino Nano (Rev3.0) (ICSP)
  J2 = Infrared Proximity Sensor

nets:
  N1: J1.pin2, 元件1.D8
  GND: 元件1.GND, J2.GND
  N2: 元件1.D3, J2.Vout
  5V: 元件1.5V, J2.Vcc
