# Fritzing sketch FixedWingPlane (saved by Fritzing 0.9.3b)
breadboards: 1
perfboards: 1

parts:
  元件1 = Arduino Nano (Rev3.0) (ICSP)
  元件3 = NRF24L01+ Breakout Board
  VCC1 = Battery
  S6 = Round Pushbutton
  J1 = Basic Servo
  J2 = Basic Servo  # not connected
  J3 = Basic Servo
  元件4 = Triple Axis Accelerometer Breakout - ADXL345
  元件5 = Arduino Nano (Rev3.0)
  J4 = Basic Servo
  J5 = Basic Servo
  J6 = Basic Servo
  元件6 = NRF24L01+ Breakout Board
  S7 = Toggle Switch [package=THT]

nets:
  GND: 元件1.GND, 元件3.GND, VCC1.-
  N1: 元件1.D6, J1.pulse
  N2: 元件1.D7, 元件3.CS
  N3: 元件1.D8, 元件3.CE
  N4: 元件1.D9, J3.pulse
  N5: 元件1.D11/MOSI, 元件3.MOSI
  N6: 元件1.D12/MISO, 元件3.MISO
  N7: 元件1.VIN, S6.leg0
  5V: 元件1.5V, 元件3.VCC
  N8: 元件1.D13/SCK, 元件3.SCK
  N9: VCC1.+, S6.leg1
  GND_2: J1.gnd, J3.gnd
  VCC: J1.vcc, J3.vcc
  GND_3: 元件4.GND, 元件4.SDO, 元件5.GND, J5.gnd
  VCC_2: 元件4.VCC, 元件5.3V3
  N10: 元件4.SDA, 元件5.A4
  N11: 元件4.SCL, 元件5.A5
  N12: 元件5.D5, J6.pulse
  N13: 元件5.D6, J4.pulse
  N14: 元件5.D7, 元件6.CS
  N15: 元件5.D8, 元件6.CE
  N16: 元件5.D9, J5.pulse
  N17: 元件5.D11/MOSI, 元件6.MOSI
  N18: 元件5.D12/MISO, 元件6.MISO
  N19: 元件5.5V, S7.COM
  N20: 元件5.D13/SCK, 元件6.SCK
  GND_4: J4.gnd, J6.gnd
  VCC_3: J4.vcc, J6.vcc
  N21: J5.vcc, S7.L1

notes:
  NRF24L01_Sender
  Left servo
  Right servo
  电调
