# Fritzing sketch LED_Testing_GuangLiFang01 (saved by Fritzing 0.9.3b)
perfboards: 1

parts:
  LED1 = LED - 5mm [color="Red (633nm)" package="5 mm [THT]"]
  LED2 = LED - 5mm [color="Red (633nm)" package="5 mm [THT]"]
  LED3 = LED - 5mm [color="Red (633nm)" package="5 mm [THT]"]
  LED4 = LED - 5mm [color="Red (633nm)" package="5 mm [THT]"]
  LED5 = LED - 5mm [color="Red (633nm)" package="5 mm [THT]"]
  LED6 = LED - 5mm [color="Red (633nm)" package="5 mm [THT]"]
  LED7 = LED - 5mm [color="Red (633nm)" package="5 mm [THT]"]
  LED8 = LED - 5mm [color="Red (633nm)" package="5 mm [THT]"]
  LED9 = LED - 5mm [color="Red (633nm)" package="5 mm [THT]"]
  LED10 = LED - 5mm [color="Red (633nm)" package="5 mm [THT]"]
  LED11 = LED - 5mm [color="Red (633nm)" package="5 mm [THT]"]
  LED12 = LED - 5mm [color="Red (633nm)" package="5 mm [THT]"]
  LED13 = LED - 5mm [color="Red (633nm)" package="5 mm [THT]"]
  LED14 = LED - 5mm [color="Red (633nm)" package="5 mm [THT]"]
  LED15 = LED - 5mm [color="Red (633nm)" package="5 mm [THT]"]
  LED16 = LED - 5mm [color="Red (633nm)" package="5 mm [THT]"]
  元件1 = Arduino Nano (Rev3.0)
  R1 = Resistor [tolerance=±5% resistance=220 package=THT]
  R2 = Resistor [tolerance=±5% resistance=220 package=THT]
  R3 = Resistor [tolerance=±5% resistance=220 package=THT]
  R4 = Resistor [tolerance=±5% resistance=220 package=THT]
  R5 = Resistor [tolerance=±5% resistance=220 package=THT]
  R6 = Resistor [tolerance=±5% resistance=220 package=THT]
  R7 = Resistor [tolerance=±5% resistance=220 package=THT]
  R8 = Resistor [tolerance=±5% resistance=220 package=THT]
  R9 = Resistor [tolerance=±5% resistance=220 package=THT]
  R10 = Resistor [tolerance=±5% resistance=220 package=THT]
  R11 = Resistor [tolerance=±5% resistance=220 package=THT]
  R12 = Resistor [tolerance=±5% resistance=220 package=THT]
  R13 = Resistor [tolerance=±5% resistance=220 package=THT]
  R14 = Resistor [tolerance=±5% resistance=220 package=THT]
  R15 = Resistor [tolerance=±5% resistance=220 package=THT]
  R16 = Resistor [tolerance=±5% resistance=220 package=THT]
  LED17 = LED - 5mm [color="Red (633nm)" package="5 mm [THT]"]  # not connected
  LED18 = LED - 5mm [color="Red (633nm)" package="5 mm [THT]"]  # not connected
  LED19 = LED - 5mm [color="Red (633nm)" package="5 mm [THT]"]  # not connected
  LED20 = LED - 5mm [color="Red (633nm)" package="5 mm [THT]"]
  LED21 = LED - 5mm [color="Red (633nm)" package="5 mm [THT]"]  # not connected
  LED22 = LED - 5mm [color="Red (633nm)" package="5 mm [THT]"]  # not connected
  LED23 = LED - 5mm [color="Red (633nm)" package="5 mm [THT]"]
  LED24 = LED - 5mm [color="Red (633nm)" package="5 mm [THT]"]
  LED25 = LED - 5mm [color="Red (633nm)" package="5 mm [THT]"]
  LED26 = LED - 5mm [color="Red (633nm)" package="5 mm [THT]"]  # not connected
  LED27 = LED - 5mm [color="Red (633nm)" package="5 mm [THT]"]
  LED28 = LED - 5mm [color="Red (633nm)" package="5 mm [THT]"]
  LED29 = LED - 5mm [color="Red (633nm)" package="5 mm [THT]"]
  LED30 = LED - 5mm [color="Red (633nm)" package="5 mm [THT]"]  # not connected
  LED31 = LED - 5mm [color="Red (633nm)" package="5 mm [THT]"]
  LED32 = LED - 5mm [color="Red (633nm)" package="5 mm [THT]"]
  LED33 = LED - 5mm [color="Red (633nm)" package="5 mm [THT]"]
  LED34 = LED - 5mm [color="Red (633nm)" package="5 mm [THT]"]
  LED35 = LED - 5mm [color="Red (633nm)" package="5 mm [THT]"]  # not connected
  LED36 = LED - 5mm [color="Red (633nm)" package="5 mm [THT]"]
  LED37 = LED - 5mm [color="Red (633nm)" package="5 mm [THT]"]
  LED38 = LED - 5mm [color="Red (633nm)" package="5 mm [THT]"]
  LED39 = LED - 5mm [color="Red (633nm)" package="5 mm [THT]"]
  LED40 = LED - 5mm [color="Red (633nm)" package="5 mm [THT]"]
  LED41 = LED - 5mm [color="Red (633nm)" package="5 mm [THT]"]
  LED42 = LED - 5mm [color="Red (633nm)" package="5 mm [THT]"]
  LED43 = LED - 5mm [color="Red (633nm)" package="5 mm [THT]"]
  LED44 = LED - 5mm [color="Red (633nm)" package="5 mm [THT]"]
  LED45 = LED - 5mm [color="Red (633nm)" package="5 mm [THT]"]
  LED46 = LED - 5mm [color="Red (633nm)" package="5 mm [THT]"]
  LED47 = LED - 5mm [color="Red (633nm)" package="5 mm [THT]"]
  LED48 = LED - 5mm [color="Red (633nm)" package="5 mm [THT]"]
  LED49 = LED - 5mm [color="Red (633nm)" package="5 mm [THT]"]
  LED50 = LED - 5mm [color="Red (633nm)" package="5 mm [THT]"]
  LED51 = LED - 5mm [color="Red (633nm)" package="5 mm [THT]"]
  LED52 = LED - 5mm [color="Red (633nm)" package="5 mm [THT]"]
  LED53 = LED - 5mm [color="Red (633nm)" package="5 mm [THT]"]
  LED54 = LED - 5mm [color="Red (633nm)" package="5 mm [THT]"]
  LED55 = LED - 5mm [color="Red (633nm)" package="5 mm [THT]"]
  LED56 = LED - 5mm [color="Red (633nm)" package="5 mm [THT]"]
  LED57 = LED - 5mm [color="Red (633nm)" package="5 mm [THT]"]
  LED58 = LED - 5mm [color="Red (633nm)" package="5 mm [THT]"]  # not connected
  LED59 = LED - 5mm [color="Red (633nm)" package="5 mm [THT]"]
  LED60 = LED - 5mm [color="Red (633nm)" package="5 mm [THT]"]
  LED61 = LED - 5mm [color="Red (633nm)" package="5 mm [THT]"]
  LED62 = LED - 5mm [color="Red (633nm)" package="5 mm [THT]"]
  LED63 = LED - 5mm [color="Red (633nm)" package="5 mm [THT]"]
  LED64 = LED - 5mm [color="Red (633nm)" package="5 mm [THT]"]

nets:
  N1: LED1.cathode, LED4.cathode, LED16.cathode
  N2: LED1.anode, R1.Pin_0
  N3: LED2.cathode, LED14.cathode
  N4: LED2.anode, R5.Pin_0
  N5: LED3.cathode, LED15.cathode
  N6: LED3.anode, R9.Pin_0
  N7: LED4.anode, R13.Pin_0
  N8: LED5.anode, R2.Pin_0
  N9: LED6.anode, R8.Pin_0
  N10: LED7.anode, R12.Pin_0
  N11: LED8.anode, R16.Pin_0
  N12: LED9.anode, R3.Pin_0
  N13: LED10.anode, R7.Pin_0
  N14: LED11.anode, R11.Pin_0
  N15: LED12.anode, R15.Pin_0
  N16: LED13.cathode, 元件1.D1/TX
  N17: LED13.anode, R4.Pin_0
  N18: LED14.anode, R6.Pin_0
  N19: LED15.anode, R10.Pin_0
  N20: LED16.anode, R14.Pin_0
  N21: 元件1.D0/RX, LED20.cathode, LED25.cathode, LED27.cathode, LED28.cathode, LED29.cathode, LED31.cathode, LED32.cathode
  N22: 元件1.D2, R1.Pin_1
  N23: 元件1.D3, R2.Pin_1
  N24: 元件1.D4, R3.Pin_1
  N25: 元件1.D5, R4.Pin_1
  N26: 元件1.D6, R5.Pin_1
  N27: 元件1.D7, R8.Pin_1
  N28: 元件1.D8, R7.Pin_1
  N29: 元件1.D9, R6.Pin_1
  N30: 元件1.D10, R9.Pin_1
  N31: 元件1.D11/MOSI, R12.Pin_1
  N32: 元件1.D12/MISO, R11.Pin_1
  N33: 元件1.A5, LED33.cathode, LED34.cathode, LED36.cathode, LED41.cathode, LED42.cathode, LED43.cathode, LED44.cathode, LED45.cathode, LED46.cathode, LED47.cathode, LED48.cathode
  N34: 元件1.A4, LED49.cathode, LED50.cathode, LED51.cathode, LED52.cathode, LED57.cathode, LED59.cathode, LED60.cathode, LED61.cathode, LED62.cathode, LED63.cathode, LED64.cathode
  N35: 元件1.A3, R14.Pin_1
  N36: 元件1.A2, R15.Pin_1
  N37: 元件1.A1, R16.Pin_1
  N38: 元件1.A0, R13.Pin_1
  N39: 元件1.D13/SCK, R10.Pin_1
  N40: LED23.cathode, LED24.cathode
  N41: LED37.cathode, LED38.cathode, LED39.cathode, LED40.cathode
  N42: LED53.cathode, LED54.cathode, LED55.cathode, LED56.cathode

notes:
  第一层
  第二层
  第三层
  第四层（底层）
  11
  12
  13
  14
  23
  24
  21
  32
  34
  33
  44
  41
  42
  43
  注释:
  ① 四层阳极16针依次和其他层阳极相连;
  ② 每层阴极串联，1~4层，分别连接Nano的[A4,A5，0，1]四个针;
  ③ 阳极16针分别连接Nano的[2,3,4,5,6,7,8,9,10,11,12,13,A0,A1,A2,A3]针
