# Fritzing sketch Laseralarmer (saved by Fritzing 0.9.3b)
breadboards: 1

parts:
  J1 = Piezo Speaker
  元件1 = Arduino Leonardo (Rev3b)
  LED1 = LED - 5mm [color="Red (633nm)" package="5 mm [THT]"]
  R1 = Resistor [tolerance=±5% resistance=220 package=THT]
  元件2 = Humidity Sensor - HIH-4030 Breakout
  LED2 = Super Flux LED blue [color=Blue]  # not connected

nets:
  GND: J1.pin1, J1.pin2, 元件1.D4/A6, 元件1.GND, LED1.anode, 元件2.GND
  N1: 元件1.D7, 元件2.OUT
  5V: 元件1.5V, 元件2.VCC
  N2: 元件1.D9_PWM/A9, R1.Pin_0
  N3: LED1.cathode, R1.Pin_1

notes:
  激光接收器
  激光发射器
