# Fritzing sketch ObjectPanel (saved by Fritzing 0.9.3b)
perfboards: 1

parts:
  Peppermill_Power_Board2 = Peppermill Power Board
  元件4 = Arduino Nano (Rev3.0) (ICSP)
  Power_plug1 = Power plug
  RHT1 = Humidity and Temperature Sensor RHT03  # not connected
  元件5 = NRF24L01+ Breakout Board
  S3 = SWITCH-MOMENTARY-2 [package=tactile_switch_tall]
  U2 = Voltage Regulator [package=sot223]

nets:
  N1: Peppermill_Power_Board2.Direction, Peppermill_Power_Board2.Speed, 元件4.3V3
  N2: Peppermill_Power_Board2.GPIO, 元件4.D4
  N3: Peppermill_Power_Board2.Ground, 元件4.D5
  N4: Peppermill_Power_Board2.VPP, 元件4.D9
  N5: Peppermill_Power_Board2.PGC, 元件4.D2
  N6: Peppermill_Power_Board2.PGD, 元件4.D3
  N7: 元件4.D1/TX, 元件5.IRQ
  N8: 元件4.D0/RX, 元件5.GND
  GND: 元件4.GND, Power_plug1.GND, U2.OUT
  N9: 元件4.VIN, S3.1, U2.ADJ
  N10: Power_plug1.VCC, S3.2
  N11: 元件5.VCC, U2.IN

notes:
  ---- Nokia 5110 LCD ----
  PGD: RST PGC: CE
  VPP: DC GND: Din
  GPIO: Clk SPEED:Vcc
  DIRECTION:BL V+:Gnd
  Vin+
  GndIn-
  Vout+
  GndOut-
