# Fritzing sketch Control4Plane (saved by Fritzing 0.9.3b)
breadboards: 1

parts:
  元件1 = Arduino Nano (Rev3.0) (ICSP)
  元件2 = Thumb Joystick
  元件3 = NRF24L01+ Breakout Board
  S1 = Pushbutton [package="[THT]"]
  VCC1 = Battery
  S6 = Round Pushbutton
  R1 = Resistor [tolerance=±5% resistance=220 package=THT]
  R2 = Resistor [tolerance=±5% resistance=220 package=THT]
  R3 = Rotary Potentiometer (Small) [maximum_resistance=100kΩ package=THT]

nets:
  GND: 元件1.GND, 元件2.GND, 元件3.GND, VCC1.-, R2.Pin_1
  N1: 元件1.D4, S1.Pin_1, S1.Pin_2, R1.Pin_0
  N2: 元件1.D7, 元件3.CS
  N3: 元件1.D8, 元件3.CE
  N4: 元件1.D11/MOSI, 元件3.MOSI
  N5: 元件1.D12/MISO, 元件3.MISO
  N6: 元件1.VIN, S6.leg0
  VCC: 元件1.5V, 元件2.VCC, 元件3.VCC, R3.leg1
  N7: 元件1.A2, R3.wiper
  N8: 元件1.A1, 元件2.VERT
  N9: 元件1.A0, 元件2.HORZ
  N10: 元件1.D13/SCK, 元件3.SCK
  N11: S1.Pin_3, S1.Pin_4
  N12: VCC1.+, S6.leg1
  N13: R1.Pin_1, R2.Pin_0

notes:
  VCC:VCC
  VER :VRX
  HOF:VRY
  SEL :SW
  GND:GND
  NRF24L01_Sender
