# Fritzing sketch NRF24L01_Sender (saved by Fritzing 0.9.3b)
breadboards: 1

parts:
  元件1 = Arduino Nano (Rev3.0) (ICSP)
  元件2 = Thumb Joystick
  元件3 = NRF24L01+ Breakout Board
  S1 = Pushbutton [package="[THT]"]
  S2 = Pushbutton [package="[THT]"]
  S3 = Pushbutton [package="[THT]"]
  S4 = Pushbutton [package="[THT]"]
  VCC1 = Battery
  S6 = Round Pushbutton

nets:
  GND: 元件1.GND, 元件2.GND, 元件3.GND, S1.Pin_3, S1.Pin_4, S2.Pin_3, S2.Pin_4, VCC1.-
  N1: 元件1.D7, 元件3.CS
  N2: 元件1.D8, 元件3.CE
  N3: 元件1.D11/MOSI, 元件3.MOSI
  N4: 元件1.D12/MISO, 元件3.MISO
  N5: 元件1.VIN, S6.leg0
  VCC: 元件1.5V, 元件2.VCC, 元件3.VCC
  N6: 元件1.A7, S4.Pin_1, S4.Pin_2
  N7: 元件1.A6, S3.Pin_1, S3.Pin_2
  N8: 元件1.A5, S2.Pin_1, S2.Pin_2
  N9: 元件1.A4, S1.Pin_1, S1.Pin_2
  N10: 元件1.A2, 元件2.VERT
  N11: 元件1.A1, 元件2.HORZ
  N12: 元件1.A0, 元件2.SEL
  N13: 元件1.D13/SCK, 元件3.SCK
  N14: S3.Pin_3, S3.Pin_4, S4.Pin_3, S4.Pin_4
  N15: VCC1.+, S6.leg1

notes:
  VCC:VCC
  VER :VRX
  HOF:VRY
  SEL :SW
  GND:GND
  NRF24L01_Sender
