# Fritzing sketch ShockLamp (saved by Fritzing 0.9.3b)
perfboards: 1

parts:
  元件4 = Arduino Pro Mini (5V)
  LED1 = RGB LED (com. cathode, rbg) [package="5 mm [THT]"]
  S2 = Toggle Switch [package=THT]
  C1 = Electrolytic Capacitor [capacitance=1µF package="100 mil [THT, electrolytic]"]
  S3 = Tilt Switch [package=THT]
  R1 = Resistor [tolerance=±5% resistance=220 package=THT]
  VCC1 = Battery

nets:
  N1: 元件4.VCC, C1.-, S3.Pin_1
  N2: 元件4.RAW, S2.L1
  N3: 元件4.GND, LED1.common_cathode, R1.Pin_0, VCC1.-
  N4: 元件4.MOSI, LED1.green_anode
  N5: 元件4.D10, LED1.blue_anode
  N6: 元件4.D9, LED1.red_anode
  N7: 元件4.D3, 元件4.D2, C1.+, S3.Pin_2, R1.Pin_1
  N8: S2.COM, VCC1.+

notes:
  震动传感器1
  震动传感器2
  全彩LED（10mm）
  七彩震动灯电路图
