# Fritzing sketch TrafficManagement01 (saved by Fritzing 0.9.3b)
perfboards: 1

parts:
  元件1 = Arduino Pro Mini (5V)
  R1 = Trimmer Potentiometer [maximum_resistance=10kΩ package=THT]
  R2 = Resistor [tolerance=±5% resistance=220 package=THT]
  R3 = Resistor [tolerance=±5% resistance=220 package=THT]
  R4 = Resistor [tolerance=±5% resistance=220 package=THT]
  LED1 = LED - 5mm [color="Green (570nm)" package="5 mm [THT]"]
  LED2 = LED - 5mm [color="Yellow (595nm)" package="5 mm [THT]"]
  LED3 = LED - 5mm [color="Red (633nm)" package="5 mm [THT]"]
  J1 = Piezo Speaker
  J2 = Basic Servo
  Lhi1 = LHi958 [package=to-39]

nets:
  N1: 元件1.GND, LED1.cathode
  N2: 元件1.VCC, R1.leg1
  N3: 元件1.D9, J2.pulse
  N4: 元件1.D6, R4.Pin_1
  N5: 元件1.D5, R3.Pin_1
  N6: 元件1.D4, R2.Pin_1
  N7: 元件1.D2, Lhi1.n.a.
  N8: R1.wiper, J1.pin2
  N9: R2.Pin_0, LED3.anode
  N10: R3.Pin_0, LED2.anode
  N11: R4.Pin_0, LED1.anode
  N12: J1.pin1, J2.gnd
