# Fritzing sketch 8x8x8_lue_LED_cube_V1.00 (saved by Fritzing 0.9.3b)
breadboards: 1

parts:
  U1 = 74HC595 SMD [package="SO16 [SMD]"]
  U2 = 74HC595 SMD [package="SO16 [SMD]"]
  U3 = 74HC595 SMD [package="SO16 [SMD]"]
  U8 = 74HC595 SMD [package="SO16 [SMD]"]
  元件1 = Arduino Nano (Rev3.0)
  R1 = Resistor [tolerance=±5% resistance=1k package=THT]  # not connected
  R2 = Resistor [tolerance=±5% resistance=1k package=THT]  # not connected
  R3 = Resistor [tolerance=±5% resistance=1k package=THT]  # not connected
  R4 = Resistor [tolerance=±5% resistance=1k package=THT]  # not connected
  R5 = Resistor [tolerance=±5% resistance=1k package=THT]
  R6 = Resistor [tolerance=±5% resistance=1k package=THT]  # not connected
  R7 = Resistor [tolerance=±5% resistance=1k package=THT]  # not connected
  R8 = Resistor [tolerance=±5% resistance=1k package=THT]  # not connected
  R9 = Resistor [tolerance=±5% resistance=1k package=THT]  # not connected
  R10 = Resistor [tolerance=±5% resistance=1k package=THT]  # not connected
  R11 = Resistor [tolerance=±5% resistance=1k package=THT]
  R12 = Resistor [tolerance=±5% resistance=1k package=THT]  # not connected
  R13 = Resistor [tolerance=±5% resistance=1k package=THT]  # not connected
  R14 = Resistor [tolerance=±5% resistance=1k package=THT]  # not connected
  R15 = Resistor [tolerance=±5% resistance=1k package=THT]  # not connected
  R16 = Resistor [tolerance=±5% resistance=1k package=THT]  # not connected
  R17 = Resistor [tolerance=±5% resistance=1k package=THT]  # not connected
  R18 = Resistor [tolerance=±5% resistance=1k package=THT]  # not connected
  R19 = Resistor [tolerance=±5% resistance=1k package=THT]
  R20 = Resistor [tolerance=±5% resistance=1k package=THT]  # not connected
  R21 = Resistor [tolerance=±5% resistance=1k package=THT]  # not connected
  R22 = Resistor [tolerance=±5% resistance=1k package=THT]  # not connected
  R23 = Resistor [tolerance=±5% resistance=1k package=THT]  # not connected
  R24 = Resistor [tolerance=±5% resistance=1k package=THT]  # not connected
  R57 = Resistor [tolerance=±5% resistance=1k package=THT]  # not connected
  R58 = Resistor [tolerance=±5% resistance=1k package=THT]  # not connected
  R59 = Resistor [tolerance=±5% resistance=1k package=THT]
  R60 = Resistor [tolerance=±5% resistance=1k package=THT]  # not connected
  R61 = Resistor [tolerance=±5% resistance=1k package=THT]  # not connected
  R62 = Resistor [tolerance=±5% resistance=1k package=THT]  # not connected
  R63 = Resistor [tolerance=±5% resistance=1k package=THT]  # not connected
  R64 = Resistor [tolerance=±5% resistance=1k package=THT]  # not connected
  R65 = Resistor [tolerance=±5% resistance=1k package=THT]
  2N2222_2222 = NPN-Transistor [package="TO92 [THT]"]
  R66 = Resistor [tolerance=±5% resistance=1k package=THT]
  FQP27P06_27P06 = Basic FET P-Channel [package="D2Pak [SMD]"]
  R67 = Resistor [tolerance=±5% resistance=1k package=THT]
  R68 = Resistor [tolerance=±5% resistance=1k package=THT]
  2N2222_2222_2 = NPN-Transistor [package="TO92 [THT]"]
  FQP27P06_27P06_2 = Basic FET P-Channel [package="D2Pak [SMD]"]
  R69 = Resistor [tolerance=±5% resistance=1k package=THT]
  R70 = Resistor [tolerance=±5% resistance=1k package=THT]
  2N2222_2222_3 = NPN-Transistor [package="TO92 [THT]"]
  FQP27P06_27P06_3 = Basic FET P-Channel [package="D2Pak [SMD]"]
  R71 = Resistor [tolerance=±5% resistance=1k package=THT]
  R72 = Resistor [tolerance=±5% resistance=1k package=THT]
  2N2222_2222_4 = NPN-Transistor [package="TO92 [THT]"]
  FQP27P06_27P06_4 = Basic FET P-Channel [package="D2Pak [SMD]"]
  part = female pin header, 2 pins [form="♀ (female)"]  # not connected
  part_2 = female pin header, 2 pins [form="♀ (female)"]  # not connected
  part_3 = female pin header, 2 pins [form="♀ (female)"]  # not connected
  part_4 = female pin header, 2 pins [form="♀ (female)"]  # not connected
  part_5 = female pin header, 2 pins [form="♀ (female)"]  # not connected
  part_6 = female pin header, 2 pins [form="♀ (female)"]  # not connected
  part_7 = female pin header, 2 pins [form="♀ (female)"]  # not connected
  part_8 = female pin header, 2 pins [form="♀ (female)"]
  part_9 = female pin header, 2 pins [form="♀ (female)"]  # not connected
  part_10 = female pin header, 2 pins [form="♀ (female)"]  # not connected
  part_11 = female pin header, 2 pins [form="♀ (female)"]  # not connected
  part_12 = female pin header, 2 pins [form="♀ (female)"]
  part_13 = female pin header, 2 pins [form="♀ (female)"]  # not connected
  part_14 = female pin header, 2 pins [form="♀ (female)"]  # not connected
  part_15 = female pin header, 2 pins [form="♀ (female)"]
  part_16 = female pin header, 2 pins [form="♀ (female)"]  # not connected
  part_17 = female pin header, 2 pins [form="♀ (female)"]  # not connected
  part_18 = female pin header, 2 pins [form="♀ (female)"]  # not connected
  part_19 = female pin header, 2 pins [form="♀ (female)"]
  part_20 = female pin header, 2 pins [form="♀ (female)"]  # not connected

nets:
  GND: U1.GND, U1.OE, U2.GND, U2.OE, U3.GND, U3.OE, 2N2222_2222.E, 2N2222_2222_2.E, 2N2222_2222_3.E, 2N2222_2222_4.E
  VCC: U1.MR, U1.VCC, U2.MR, U2.VCC, U3.MR, U3.VCC
  N1: U1.SH_CP, U2.SH_CP, U3.SH_CP
  N2: U1.ST_CP, U2.ST_CP, U3.ST_CP
  N3: U1.DS, U2.Q7'
  N4: U2.DS, U3.Q7'
  N5: U3.DS, U8.Q7'
  GND_2: U8.GND, U8.OE, 元件1.GND
  VCC_2: U8.MR, U8.VCC, 元件1.5V, R66.Pin_1, FQP27P06_27P06.drain, R68.Pin_1, FQP27P06_27P06_2.drain, R70.Pin_1, FQP27P06_27P06_3.drain, R72.Pin_1, FQP27P06_27P06_4.drain
  N6: U8.SH_CP, 元件1.D12/MISO
  N7: U8.ST_CP, 元件1.D13/SCK
  N8: U8.DS, 元件1.D11/MOSI
  N9: 元件1.D2, R65.Pin_1
  N10: 元件1.D3, R67.Pin_1
  N11: 元件1.D4, R69.Pin_1
  N12: 元件1.D10, R71.Pin_1
  N13: R5.Pin_1, part_8.pin2
  N14: R11.Pin_1, part_12.pin2
  N15: R19.Pin_1, part_15.pin2
  N16: R59.Pin_1, part_19.pin2
  N17: R65.Pin_0, 2N2222_2222.B
  N18: 2N2222_2222.C, FQP27P06_27P06.Gate
  N19: R67.Pin_0, 2N2222_2222_2.B
  N20: 2N2222_2222_2.C, FQP27P06_27P06_2.Gate
  N21: R69.Pin_0, 2N2222_2222_3.B
  N22: 2N2222_2222_3.C, FQP27P06_27P06_3.Gate
  N23: R71.Pin_0, 2N2222_2222_4.B
  N24: 2N2222_2222_4.C, FQP27P06_27P06_4.Gate

notes:
  D5-D9省略
  省略中间的4组
